# Fritzing sketch smartWasteDisposalSystem (saved by Fritzing 0.9.3b)
breadboards: 1

parts:
  Componente1 = Arduino Uno (Rev3) - ICSP
  hc-sr1 = hc-sr04
  Componente2 = HC-SR501 Body Sensor Module
  LED1 = smd LED [color="Red (633nm)" package="1206 [SMD]"]
  LED2 = smd LED [color="Green (555nm)" package="1206 [SMD]"]
  S1 = Pushbutton [package="[SMD]"]
  S2 = Pushbutton [package="[SMD]"]
  Display1 = LCD screen 16x2 IIC [part_number=101290]
  T1 = LM35 Temperature Sensor [package="TO92 [THT]"]
  J1 = Basic Servo
  R1 = Resistor [tolerance=±10% resistance=220 package="2512 [SMD]"]
  R2 = Resistor [tolerance=±10% resistance=220 package="2512 [SMD]"]
  R3 = Resistor [tolerance=±5% resistance=10k package="0603 [SMD]"]
  R4 = Resistor [tolerance=±5% resistance=10k package="0603 [SMD]"]

nets:
  N1: Componente1.A0, T1.Vout
  N2: Componente1.A4/SDA, Display1.SDA
  N3: Componente1.A5/SCL, Display1.SCL
  N4: Componente1.ICSP_MISO, Componente1.D12/MISO, hc-sr1.Trig
  VCC: Componente1.5V, hc-sr1.VCC, Componente2.VCC, S1.Pin_1, S1.Pin_2, S2.Pin_1, S2.Pin_2, Display1.VCC, T1.+Vs, J1.vcc
  N5: Componente1.D9_PWM, J1.pulse
  N6: Componente1.D13/SCK, hc-sr1.Echo
  GND: Componente1.GND, hc-sr1.GND, Componente2.GND, Display1.GND, T1.GND, J1.gnd, R1.Pin_0, R2.Pin_0, R3.Pin_0, R4.Pin_0
  N7: Componente1.D2, LED2.anode
  N8: Componente1.D3_PWM, LED1.anode
  N9: Componente1.D4, S1.Pin_3, S1.Pin_4, R4.Pin_1
  N10: Componente1.D5_PWM, S2.Pin_3, S2.Pin_4, R3.Pin_1
  N11: Componente1.D6_PWM, Componente2.OUT
  N12: LED1.cathode, R2.Pin_1
  N13: LED2.cathode, R1.Pin_1

custom parts:
  HC-SR501 Body Sensor Module: Pyroelectric Infrared PIR Motion Sensor Detector Module
  LCD screen 16x2 IIC: LCD screen with HD44780 controller enables showing text, symbols, value or anything else that comes from Croduino/Arduino. It is capable of showing 16 symbols in two lines and therefore can be used in many projects that need to send clearly visible and legible output information.. • Color of symbols: White • Backlight: Blue • Dimensions: 80 x 36 x 12 mm • Screen dimensions: 64.5 x 16 mm •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
